// Digital circuit ex3.dig as structural Verilog
module ex3 (
  input  [1:0] A,
  input  [1:0] B,
  output Y
);

  wire and_1_out, and_2_out, and_3_out, and_4_out, and_5_out, and_6_out, and_7_out, and_8_out, Case1, Case2,
       Case3, Case4, Case5, Case6, not_1_out, not_2_out, or_1_out, or_2_out;

  and and_1 (and_1_out, ~A[1], ~B[1], ~B[0]);  // And
  and and_2 (and_2_out, ~A[0], ~B[1], ~B[0]);  // And
  and and_3 (and_3_out, A[1], B[0]);
  and and_4 (and_4_out, ~A[0], ~B[1]);  // And
  and and_5 (and_5_out, A[1], A[0]);
  and and_6 (and_6_out, ~B[1], ~B[0]);  // And
  and and_7 (and_7_out, A[1], A[0], B[0]);
  not not_1 (not_1_out, B[1]);
  and and_8 (and_8_out, A[1], A[0], B[1]);
  not not_2 (not_2_out, B[0]);
  and and_9 (Case1, A[0], and_1_out);
  and and_10 (Case2, A[1], and_2_out);
  and and_11 (Case3, and_3_out, and_4_out);
  and and_12 (Case4, and_5_out, and_6_out);
  and and_13 (Case5, and_7_out, not_1_out);
  and and_14 (Case6, and_8_out, not_2_out);
  or or_1 (or_1_out, Case1, Case2, Case3);
  or or_2 (or_2_out, Case4, Case5, Case6);
  or or_3 (Y, or_1_out, or_2_out);
endmodule

/* Test case EX3 Test:
A B Y 

 0b00 0b00 0
 0b00 0b01 0
 0b00 0b10 0
 0b00 0b11 0
 0b01 0b00 1
 0b01 0b01 0
 0b01 0b10 0
 0b01 0b11 0
 0b10 0b00 1
 0b10 0b01 1
 0b10 0b10 0
 0b10 0b11 0
 0b11 0b00 1
 0b11 0b01 1
 0b11 0b10 1
 0b11 0b11 0
*/
