// Digital circuit Lab02.dig as structural Verilog
module Lab02 (
  input  B,
  input  C,
  input  A,
  input  D,
  output Fa,
  output Fb,
  output Fc,
  output Fd,
  output Fe,
  output Fg,
  output Ff
);

  wire and_1_out, and_2_out, and_3_out, and_4_out, and_5_out, and_6_out, and_7_out, and_8_out, and_9_out,
       and_10_out, and_11_out, and_12_out, and_13_out, and_14_out, and_15_out, and_16_out, and_17_out,
       and_18_out, and_19_out, and_20_out, and_21_out, and_22_out, and_23_out, and_24_out, and_25_out,
       nor_1_out, nor_2_out, nor_3_out, nor_4_out, nor_5_out, nor_6_out, nor_7_out, nor_8_out, or_4_out,
       or_5_out;

  Seven_Seg seven_seg_1 (.a(1'b1), .b(1'b0), .c(1'b1), .d(1'b1), .e(1'b1), .f(1'b1), .g(1'b1), .dp(1'b0));
  Seven_Seg seven_seg_2 (.a(Fa), .b(Fb), .c(Fc), .d(Fd), .e(Fe), .f(Ff), .g(Fg), .dp(1'b0));
  nor nor_1 (nor_1_out, B, D);
  and and_1 (and_1_out, A, ~B, ~C);  // And
  and and_2 (and_2_out, B, C);
  and and_3 (and_3_out, ~A, C, D);  // And
  and and_4 (and_4_out, ~A, B, D);  // And
  nor nor_2 (nor_2_out, A, B);
  nor nor_3 (nor_3_out, B, D);
  nor nor_4 (nor_4_out, A, C, D);
  and and_5 (and_5_out, ~A, C, D);  // And
  and and_6 (and_6_out, A, ~C, D);  // And
  and and_7 (and_7_out, ~A, B);  // And
  and and_8 (and_8_out, A, ~B);  // And
  and and_9 (and_9_out, ~C, D);  // And
  nor nor_5 (nor_5_out, A, C);
  and and_10 (and_10_out, ~A, D);  // And
  and and_11 (and_11_out, A, ~C);  // And
  nor nor_6 (nor_6_out, B, C, D);
  and and_12 (and_12_out, B, ~C, D);  // And
  and and_13 (and_13_out, A, ~B, D);  // And
  and and_14 (and_14_out, ~A, ~B, C);  // And
  and and_15 (and_15_out, B, C, ~D);  // And
  nor nor_7 (nor_7_out, B, D);
  and and_16 (and_16_out, A, B);
  and and_17 (and_17_out, A, C);
  and and_18 (and_18_out, C, ~D);  // And
  and and_19 (and_19_out, A, ~B);  // And
  and and_20 (and_20_out, A, C);
  and and_21 (and_21_out, B, C, ~D);  // And
  nor nor_8 (nor_8_out, A, C, D);
  and and_22 (and_22_out, ~A, B, ~C);  // And
  and and_23 (and_23_out, B, ~C);  // And
  and and_24 (and_24_out, C, ~D);  // And
  and and_25 (and_25_out, ~A, ~B, C);  // And
  or or_1 (Fa, nor_1_out, and_1_out, and_2_out, and_3_out, and_4_out);
  or or_2 (Fb, nor_2_out, nor_3_out, nor_4_out, and_5_out, and_6_out);
  or or_3 (Fc, and_7_out, and_8_out, and_9_out, nor_5_out, and_10_out);
  or or_4 (or_4_out, and_11_out, nor_6_out, and_12_out);
  or or_5 (or_5_out, and_13_out, and_14_out, and_15_out);
  or or_6 (Fe, nor_7_out, and_16_out, and_17_out, and_18_out);
  or or_7 (Ff, and_19_out, and_20_out, and_21_out, nor_8_out, and_22_out);
  or or_8 (Fg, A, and_23_out, and_24_out, and_25_out);
  or or_9 (Fd, or_4_out, or_5_out);

  // Other names for the same wires on the sheet: C1 = Fa; C2 = Fb; C3 = Fc; C4 = Fd; C5 = Fe; C6 = Ff; C7 = Fg
endmodule
