// Digital circuit register-file.dig as structural Verilog
module register_file (
  input  [4:0] ReadReg1,
  input  [4:0] ReadReg2,
  input  [4:0] WriteReg,
  input  [31:0] WriteData,
  input  RegWrite,
  input  Clock,
  output [31:0] ReadData1,
  output [31:0] ReadData2
);

  wire _0, _1, _2, _3, _4, _5, _6, _7, _8, _9, _10, _11, _12, _13, _14, _15, _16, _17, _18, _19, _20, _21,
       _22, _23, _24, _25, _26, _27, _28, _29, _30, _31, and_1_out, and_2_out, and_3_out, and_4_out,
       and_5_out, and_6_out, and_7_out, and_8_out, and_9_out, and_10_out, and_11_out, and_12_out, and_13_out,
       and_14_out, and_15_out, and_16_out, and_17_out, and_18_out, and_19_out, and_20_out, and_21_out,
       and_22_out, and_23_out, and_24_out, and_25_out, and_26_out, and_27_out, and_28_out, and_29_out,
       and_30_out, and_31_out, and_32_out;
  wire [31:0] Eight, Eighteen, Eleven, Fifteen, Five, Four, Fourteen, Nine, Nineteen, One, Seven, Seventeen,
       Six, Sixteen, Ten, Thirteen, Thirty, Thirty_One, Three, Twelve, Twenty, Twenty_Eight, Twenty_Five,
       Twenty_Four, Twenty_Nine, Twenty_One, Twenty_Seven, Twenty_Six, Twenty_Three, Twenty_Two, Two, Zero;

  Demultiplexer #(.Selector_Bits(5)) demultiplexer_1 (
    .sel(WriteReg), .in(1'b1), .out_0(_0), .out_1(_1), .out_2(_2), .out_3(_3), .out_4(_4), .out_5(_5),
    .out_6(_6), .out_7(_7), .out_8(_8), .out_9(_9), .out_10(_10), .out_11(_11), .out_12(_12), .out_13(_13),
    .out_14(_14), .out_15(_15), .out_16(_16), .out_17(_17), .out_18(_18), .out_19(_19), .out_20(_20),
    .out_21(_21), .out_22(_22), .out_23(_23), .out_24(_24), .out_25(_25), .out_26(_26), .out_27(_27),
    .out_28(_28), .out_29(_29), .out_30(_30), .out_31(_31));
  and and_1 (and_1_out, RegWrite, _0);
  and and_2 (and_2_out, RegWrite, _1);
  and and_3 (and_3_out, RegWrite, _2);
  and and_4 (and_4_out, RegWrite, _3);
  and and_5 (and_5_out, RegWrite, _4);
  and and_6 (and_6_out, RegWrite, _5);
  and and_7 (and_7_out, RegWrite, _6);
  and and_8 (and_8_out, RegWrite, _7);
  and and_9 (and_9_out, RegWrite, _8);
  and and_10 (and_10_out, RegWrite, _9);
  and and_11 (and_11_out, RegWrite, _10);
  and and_12 (and_12_out, RegWrite, _11);
  and and_13 (and_13_out, RegWrite, _12);
  and and_14 (and_14_out, RegWrite, _13);
  and and_15 (and_15_out, RegWrite, _14);
  and and_16 (and_16_out, RegWrite, _15);
  and and_17 (and_17_out, RegWrite, _16);
  and and_18 (and_18_out, RegWrite, _17);
  and and_19 (and_19_out, RegWrite, _18);
  and and_20 (and_20_out, RegWrite, _19);
  and and_21 (and_21_out, RegWrite, _20);
  and and_22 (and_22_out, RegWrite, _21);
  and and_23 (and_23_out, RegWrite, _22);
  and and_24 (and_24_out, RegWrite, _23);
  and and_25 (and_25_out, RegWrite, _24);
  and and_26 (and_26_out, RegWrite, _25);
  and and_27 (and_27_out, RegWrite, _26);
  and and_28 (and_28_out, RegWrite, _27);
  and and_29 (and_29_out, RegWrite, _28);
  and and_30 (and_30_out, RegWrite, _29);
  and and_31 (and_31_out, RegWrite, _30);
  and and_32 (and_32_out, RegWrite, _31);
  Register #(.Bits(32)) Register_0 (.D({32{1'b0}}), .C(Clock), .en(and_1_out), .Q(Zero));
  Register #(.Bits(32)) Register_1 (.D(WriteData), .C(Clock), .en(and_2_out), .Q(One));
  Register #(.Bits(32)) Register_2 (.D(WriteData), .C(Clock), .en(and_3_out), .Q(Two));
  Register #(.Bits(32)) Register_3 (.D(WriteData), .C(Clock), .en(and_4_out), .Q(Three));
  Register #(.Bits(32)) Register_4 (.D(WriteData), .C(Clock), .en(and_5_out), .Q(Four));
  Register #(.Bits(32)) Register_5 (.D(WriteData), .C(Clock), .en(and_6_out), .Q(Five));
  Register #(.Bits(32)) Register_6 (.D(WriteData), .C(Clock), .en(and_7_out), .Q(Six));
  Register #(.Bits(32)) Register_7 (.D(WriteData), .C(Clock), .en(and_8_out), .Q(Seven));
  Register #(.Bits(32)) Register_8 (.D(WriteData), .C(Clock), .en(and_9_out), .Q(Eight));
  Register #(.Bits(32)) Register_9 (.D(WriteData), .C(Clock), .en(and_10_out), .Q(Nine));
  Register #(.Bits(32)) Register_10 (.D(WriteData), .C(Clock), .en(and_11_out), .Q(Ten));
  Register #(.Bits(32)) Register_11 (.D(WriteData), .C(Clock), .en(and_12_out), .Q(Eleven));
  Register #(.Bits(32)) Register_12 (.D(WriteData), .C(Clock), .en(and_13_out), .Q(Twelve));
  Register #(.Bits(32)) Register_13 (.D(WriteData), .C(Clock), .en(and_14_out), .Q(Thirteen));
  Register #(.Bits(32)) Register_14 (.D(WriteData), .C(Clock), .en(and_15_out), .Q(Fourteen));
  Register #(.Bits(32)) Register_15 (.D(WriteData), .C(Clock), .en(and_16_out), .Q(Fifteen));
  Register #(.Bits(32)) Register_16 (.D(WriteData), .C(Clock), .en(and_17_out), .Q(Sixteen));
  Register #(.Bits(32)) Register_17 (.D(WriteData), .C(Clock), .en(and_18_out), .Q(Seventeen));
  Register #(.Bits(32)) Register_18 (.D(WriteData), .C(Clock), .en(and_19_out), .Q(Eighteen));
  Register #(.Bits(32)) Register_19 (.D(WriteData), .C(Clock), .en(and_20_out), .Q(Nineteen));
  Register #(.Bits(32)) Register_20 (.D(WriteData), .C(Clock), .en(and_21_out), .Q(Twenty));
  Register #(.Bits(32)) Register_21 (.D(WriteData), .C(Clock), .en(and_22_out), .Q(Twenty_One));
  Register #(.Bits(32)) Register_22 (.D(WriteData), .C(Clock), .en(and_23_out), .Q(Twenty_Two));
  Register #(.Bits(32)) Register_23 (.D(WriteData), .C(Clock), .en(and_24_out), .Q(Twenty_Three));
  Register #(.Bits(32)) Register_24 (.D(WriteData), .C(Clock), .en(and_25_out), .Q(Twenty_Four));
  Register #(.Bits(32)) Register_25 (.D(WriteData), .C(Clock), .en(and_26_out), .Q(Twenty_Five));
  Register #(.Bits(32)) Register_26 (.D(WriteData), .C(Clock), .en(and_27_out), .Q(Twenty_Six));
  Register #(.Bits(32)) Register_27 (.D(WriteData), .C(Clock), .en(and_28_out), .Q(Twenty_Seven));
  Register #(.Bits(32)) Register_28 (.D(WriteData), .C(Clock), .en(and_29_out), .Q(Twenty_Eight));
  Register #(.Bits(32)) Register_29 (.D(WriteData), .C(Clock), .en(and_30_out), .Q(Twenty_Nine));
  Register #(.Bits(32)) Register_30 (.D(WriteData), .C(Clock), .en(and_31_out), .Q(Thirty));
  Register #(.Bits(32)) Register_31 (.D(WriteData), .C(Clock), .en(and_32_out), .Q(Thirty_One));
  Multiplexer #(.Bits(32), .Selector_Bits(5)) multiplexer_1 (
    .sel(ReadReg1), .in_0(Zero), .in_1(One), .in_2(Two), .in_3(Three), .in_4(Four), .in_5(Five), .in_6(Six),
    .in_7(Seven), .in_8(Eight), .in_9(Nine), .in_10(Ten), .in_11(Eleven), .in_12(Twelve), .in_13(Thirteen),
    .in_14(Fourteen), .in_15(Fifteen), .in_16(Sixteen), .in_17(Seventeen), .in_18(Eighteen),
    .in_19(Nineteen), .in_20(Twenty), .in_21(Twenty_One), .in_22(Twenty_Two), .in_23(Twenty_Three),
    .in_24(Twenty_Four), .in_25(Twenty_Five), .in_26(Twenty_Six), .in_27(Twenty_Seven), .in_28(Twenty_Eight),
    .in_29(Twenty_Nine), .in_30(Thirty), .in_31(Thirty_One), .out(ReadData1));
  Multiplexer #(.Selector_Bits(5), .Bits(32)) multiplexer_2 (
    .sel(ReadReg2), .in_0(Zero), .in_1(One), .in_2(Two), .in_3(Three), .in_4(Four), .in_5(Five), .in_6(Six),
    .in_7(Seven), .in_8(Eight), .in_9(Nine), .in_10(Ten), .in_11(Eleven), .in_12(Twelve), .in_13(Thirteen),
    .in_14(Fourteen), .in_15(Fifteen), .in_16(Sixteen), .in_17(Seventeen), .in_18(Eighteen),
    .in_19(Nineteen), .in_20(Twenty), .in_21(Twenty_One), .in_22(Twenty_Two), .in_23(Twenty_Three),
    .in_24(Twenty_Four), .in_25(Twenty_Five), .in_26(Twenty_Six), .in_27(Twenty_Seven), .in_28(Twenty_Eight),
    .in_29(Twenty_Nine), .in_30(Thirty), .in_31(Thirty_One), .out(ReadData2));

  // Other names for the same wires on the sheet: Clk = Clock; RW = RegWrite; WD[31:0] = WriteData; WR[4:0] = WriteReg
endmodule

/* Test case Register File Test:
WriteReg WriteData RegWrite Clock ReadReg1 ReadReg2 ReadData1 ReadData2

# $1 = 25
1 25 1 C 1 0 25 0

# $2 = 30
2 30 1 C 0 2 0 30

# $(N+1) = (N+1)
loop(N, 30)
	(N+1) (N+1) 1 C (N+1) (N) (N+1) (N)
end loop

# $(N+1) = N-60
loop(N, 30)
	(N+1) (N-60) 1 C (N+1) (N+1) (N-60) (N-60)
end loop

# Try writing to $0. This should not write anything
0 25 1 C 0 0 0 0

# try writing when RegWrite = 0
# (the registers should still have their old values)
loop(N, 30)
	(N+1) (N+80) 0 C (N+1) (N+1) (N-60) (N-60)
end loop
*/
